// Logisim project LogismDiagrams.circ as structural Verilog: 1 circuit, main circuit main
module main (
  input  in_1,
  input  in_2,
  input  in_3,
  input  in_4,
  input  in_5,
  input  in,
  input  in_7,
  input  sel,
  input  in_9,
  input  a,
  input  sel_2,
  input  in_6,
  input  b,
  input  sel_3,
  output out_15,
  output out_16,
  output b_2,
  output out_18,
  output a_2,
  output out_20,
  output a_3,
  output out_22,
  output out_23,
  output b_3
);

  wire and_1_out, and_2_out, and_3_out, nand_1_out, nand_2_out, not_1_out, not_2_out, not_3_out, not_4_out,
       not_5_out, or_1_out, or_4_out;

  not not_1 (not_1_out, in_1);
  not not_2 (not_2_out, in_4);
  or or_1 (or_1_out, in_5, in_7);
  and and_1 (and_1_out, in_9, in_5);
  not not_3 (not_3_out, sel_3);
  and and_2 (and_2_out, not_1_out, in_4);
  and and_3 (and_3_out, in_1, not_2_out);
  and and_4 (out_18, or_1_out, and_1_out);
  and and_5 (out_20, a, not_3_out);
  and and_6 (out_23, b, sel_3);
  or or_2 (out_15, and_2_out, and_3_out);
  or or_3 (out_22, out_20, out_23);
  nand nand_1 (nand_1_out, in_2, in_2, in_2);
  nand nand_2 (nand_2_out, in_3, in_3);
  or or_4 (or_4_out, in, in);
  and and_7 (b_2, or_4_out, sel);
  not not_4 (not_4_out, sel_2);
  nand nand_3 (out_16, nand_1_out, nand_2_out);
  not not_5 (not_5_out, b_2);
  and and_8 (a_3, not_4_out, in_6);
  and and_9 (b_3, sel_2, in_6);
  or or_5 (a_2, not_5_out, sel);

  // Notes on the sheet:
  //   My first XOR
  //   MUX - failed design
  //   MUX attempt #2
  //   OR
  //   DMUX - failed design
  //   DMUX attempt #2
endmodule
